# Fritzing sketch Breadboard Diagram (saved by Fritzing 0.9.3b)
breadboards: 1

parts:
  Part1 = Photon
  R2 = Resistor [tolerance=±5% resistance=220 package=THT]
  S1 = Pushbutton [package="[THT]"]
  S2 = Pushbutton [package="[THT]"]
  S3 = Pushbutton [package="[THT]"]
  S4 = Pushbutton [package="[THT]"]
  S5 = Pushbutton [package="[THT]"]
  R4 = Resistor [tolerance=±5% resistance=220 package=THT]
  R5 = Resistor [tolerance=±5% resistance=220 package=THT]
  R6 = Resistor [tolerance=±5% resistance=220 package=THT]
  R7 = Resistor [tolerance=±5% resistance=220 package=THT]

nets:
  N1: Part1.GND, R2.Pin_0, R4.Pin_0, R5.Pin_0, R6.Pin_0, R7.Pin_0
  N2: Part1.D0, S1.Pin_1, S1.Pin_2, R7.Pin_1
  N3: Part1.D1, R2.Pin_1, S4.Pin_1, S4.Pin_2
  N4: Part1.D2, S2.Pin_1, S2.Pin_2, R4.Pin_1
  N5: Part1.D3, S5.Pin_1, S5.Pin_2, R6.Pin_1
  N6: Part1.D4, S3.Pin_1, S3.Pin_2, R5.Pin_1
  N7: Part1.3V3, S1.Pin_3, S1.Pin_4, S2.Pin_3, S2.Pin_4, S3.Pin_3, S3.Pin_4, S4.Pin_3, S4.Pin_4, S5.Pin_3, S5.Pin_4
